# Fritzing sketch schematic (saved by Fritzing 0.9.4)

parts:
  Part1 = Arduino Uno (Rev3)
  Part2 = KY-008 Laser Transmitter Module [package="Breakout board"]
  Mod1 = laser receiver [package=THT]

nets:
  N1: Part1.D3_PWM, Mod1.pin2
  N2: Part1.3V3, Mod1.pin3
  N3: Part1.5V, Part2.S
  N4: Part1.GND, Part2.-, Mod1.pin1

custom parts:
  KY-008 Laser Transmitter Module: Laser Transmitter module KY-008 for Arduino, emits a dot shaped red laser beam.
  laser receiver: Generic non modulated laser receiver module.
